# Fritzing sketch dingdongditch (saved by Fritzing 0.9.3b)
breadboards: 1

parts:
  Raspberry_Pi_B_rev1 = Raspberry Pi B rev1
  R1 = Resistor [tolerance=±5% resistance=2.15k package="1206 [SMD]"]
  R2 = Resistor [tolerance=±5% resistance=130 package="1206 [SMD]"]
  Doorbell = Pushbutton [package=THT]
  Vishay = Optocoupler, AC input [part_number=SFH620AGB package=DIP-4]
  16V_AC_10VA_Transformer = Transformer [package=transformer]

nets:
  N1: Raspberry_Pi_B_rev1.GND, Vishay.Pin_3
  N2: Raspberry_Pi_B_rev1.GPIO_21, Vishay.Pin_4
  N3: R1.Pin_0, Doorbell.leg0
  N4: R1.Pin_1, R2.Pin_1, Vishay.Pin_1
  GND: R2.Pin_0, Vishay.Pin_2, 16V_AC_10VA_Transformer.4
  N5: Doorbell.leg1, 16V_AC_10VA_Transformer.3

custom parts:
  Optocoupler, AC input: Optocoupler, Phototransistor Output, AC Input, 5300 VRMS
